# Fritzing sketch flyintelbot_core (saved by Fritzing 0.9.4)
breadboards: 1

parts:
  Raspberry_Pi_1 = Raspberry Pi 3 [part_number=RPI-3-V1.2]  # not connected
  ADC1 = MCP3008 [package=dil16]
  Part2 = Monster Moto Shield  # not connected
  M1 = DC Motor  # not connected
  M2 = DC Motor  # not connected
  M3 = DC Motor  # not connected
  M4 = DC Motor  # not connected
  J2 = Infrared Proximity Sensor
  J3 = Infrared Proximity Sensor
  J4 = Infrared Proximity Sensor
  J5 = Infrared Proximity Sensor
  Disp1 = LBT2088AH [part_number=LBT2088AH]  # not connected
  U1 = MAX7219 [package=dil24]  # not connected
  J6 = Infrared Proximity Sensor

nets:
  N1: ADC1.CH0, J3.Vout
  N2: ADC1.CH1, J6.Vout
  N3: ADC1.CH2, J2.Vout
  N4: ADC1.CH3, J5.Vout
  N5: ADC1.CH4, J4.Vout
